// Logisim project cpu.circ as structural Verilog: 2 circuits, main circuit main
module main (
  input  [31:0] INSTRUCTION,
  input  CLOCK,
  output [31:0] FETCH_ADDRESS,
  output [31:0] s0_Value,
  output [31:0] s1_Value,
  output [31:0] s2_Value,
  output [31:0] ra_Value,
  output [31:0] sp_Value
);

  wire ALUsrc, and_1_out, and_2_out, beq, bne, equal, ExtOp, jump, jumpreg, main_2_signed_overflow, MemtoReg,
       MemWr, RegDst, RegWr;
  wire [3:0] ALUctr;
  wire [4:0] multiplexer_5_out;
  wire [15:0] IMM16;
  wire [25:0] IMM26;
  wire [31:0] adder_1_out, adder_2_out, bit_extender_1_out, bit_extender_2_out, bit_extender_3_out,
       bit_extender_4_out, main_1_read_data_2, main_2_result, main_3_p5, multiplexer_1_out,
       multiplexer_2_out, multiplexer_3_out, multiplexer_4_out, multiplexer_6_out, multiplexer_7_out,
       multiplexer_8_out, RS_value;

  assign bit_extender_1_out = {{16{1'b0}}, IMM16};  // Bit_Extender bit_extender_1
  Adder #(.width(32)) adder_1 (.a(FETCH_ADDRESS), .b(32'h4), .out(adder_1_out));  // open: cin, cout
  Adder #(.width(32)) adder_2 (.a(adder_1_out), .b(bit_extender_1_out), .out(adder_2_out));  // open: cin, cout
  Multiplexer #(.width(32), .enable("false")) multiplexer_1 (
    .in0(adder_1_out), .in1(adder_2_out), .out(multiplexer_1_out), .sel(and_1_out));
  and and_1 (and_1_out, beq, equal);
  Multiplexer #(.width(32), .enable("false")) multiplexer_2 (
    .in0(multiplexer_1_out), .in1(adder_2_out), .out(multiplexer_2_out), .sel(and_2_out));
  and and_2 (and_2_out, bne, ~equal);  // AND_Gate
  assign bit_extender_2_out = {{6{1'b0}}, IMM26};  // Bit_Extender bit_extender_2
  Multiplexer #(.width(32), .enable("false")) multiplexer_3 (
    .in0(multiplexer_2_out), .in1(bit_extender_2_out), .out(multiplexer_3_out), .sel(jump));
  Multiplexer #(.width(32), .enable("false")) multiplexer_4 (
    .in0(multiplexer_3_out), .in1(RS_value), .out(multiplexer_4_out), .sel(jumpreg));
  Register #(.width(32)) PC (.D(multiplexer_4_out), .Q(FETCH_ADDRESS), .clk(CLOCK));  // open: en, clr
  Multiplexer #(.width(5)) multiplexer_5 (
    .in0(INSTRUCTION[15:11]), .in1(INSTRUCTION[20:16]), .out(multiplexer_5_out), .sel(RegDst));  // open: en
  assign bit_extender_3_out = {{16{1'b0}}, IMM16};  // Bit_Extender bit_extender_3
  assign bit_extender_4_out = {{16{IMM16[15]}}, IMM16};  // Bit_Extender bit_extender_4
  controller_circ controller_circ_1 (
    .RegDst(RegDst), .RegWr(RegWr), .ExtOp(ExtOp), .ALUsrc(ALUsrc), .ALUctr(ALUctr), .MemWr(MemWr),
    .MemtoReg(MemtoReg), .beq(beq), .bne(bne), .jump(jump), .jumpreg(jumpreg));  // open: in_1, in_2
  regfile_main main_1 (
    .Read_Register_1(INSTRUCTION[10:6]), .Read_Register_2(INSTRUCTION[15:11]),
    .Write_Register(multiplexer_5_out), .Write_Data(multiplexer_8_out), .Write_Enable(RegWr), .Clock(CLOCK),
    .Read_Data_1(RS_value), .Read_Data_2(main_1_read_data_2), .s0_Value(s0_Value), .s1_Value(s1_Value),
    .s2_Value(s2_Value), .ra_Value(ra_Value), .sp_Value(sp_Value));
  Multiplexer #(.width(32), .enable("false")) multiplexer_6 (
    .in0(bit_extender_3_out), .in1(bit_extender_4_out), .out(multiplexer_6_out), .sel(ExtOp));
  Multiplexer #(.width(32), .enable("false")) multiplexer_7 (
    .in0(main_1_read_data_2), .in1(multiplexer_6_out), .out(multiplexer_7_out), .sel(ALUsrc));
  LED led_1 (.in(main_2_signed_overflow));
  alu_main main_2 (
    .Switch(ALUctr), .X(RS_value), .Equal(equal), .Result(main_2_result),
    .Signed_Overflow(main_2_signed_overflow), .Y(multiplexer_7_out));
  // mem_main main_3: pin names not known; wires that end beside it: main_2_result, main_1_read_data_2, MemWr, CLOCK, main_3_p5
  Multiplexer #(.width(32), .enable("false")) multiplexer_8 (
    .in0(main_2_result), .in1(main_3_p5), .out(multiplexer_8_out), .sel(MemtoReg));

  // Other names for the same wires on the sheet: clk = CLOCK; fetch_addr[31:0] = FETCH_ADDRESS;
  //   opcode[5:0] = INSTRUCTION[5:0]; RS[4:0] = INSTRUCTION[10:6]; RT[4:0] = INSTRUCTION[15:11];
  //   RD[4:0] = INSTRUCTION[20:16]; shamt[4:0] = INSTRUCTION[25:21]; funct[5:0] = INSTRUCTION[31:26];
  //   ra[31:0] = ra_Value; s0[31:0] = s0_Value; s1[31:0] = s1_Value; s2[31:0] = s2_Value; sp[31:0] = sp_Value

  // Notes on the sheet:
  //   Output
  //   These are outputs/inputs from run.circ
  //   Inputs
  //   These are DEBUG/TEST outputs from your circuit.
  //   4mux to put 16 in or shift amount
endmodule

module controller_circ (
  input  [5:0] in_1,
  input  [5:0] in_2,
  output RegDst,
  output RegWr,
  output ExtOp,
  output ALUsrc,
  output [3:0] ALUctr,
  output MemWr,
  output MemtoReg,
  output beq,
  output bne,
  output jump,
  output jumpreg
);

  wire isadd, isaddi, isaddiu, isaddu, isand, isandi, isjal, isjr, islui, isor, isori, issll, isslt, isslti,
       issltiu, issltu, issra, issrl, issub, issubu, or_4_out, or_5_out, or_6_out, or_7_out, or_8_out,
       or_9_out;
  wire [3:0] multiplexer_1_out, multiplexer_2_out, multiplexer_3_out, multiplexer_4_out, multiplexer_5_out,
       multiplexer_6_out, multiplexer_7_out, multiplexer_8_out, multiplexer_9_out, multiplexer_10_out,
       multiplexer_11_out;

  and and_1 (RegDst, ~in_1[2], ~in_1[2], ~in_1[2], ~in_1[3], ~in_1[4], ~in_1[5]);  // AND_Gate
  and and_2 (isaddi, ~in_1[2], ~in_1[2], ~in_1[2], in_1[3], ~in_1[4], ~in_1[5]);  // AND_Gate
  and and_3 (isaddiu, in_1[2], ~in_1[2], ~in_1[2], in_1[3], ~in_1[4], ~in_1[5]);  // AND_Gate
  and and_4 (isandi, ~in_1[2], ~in_1[2], in_1[2], in_1[3], ~in_1[4], ~in_1[5]);  // AND_Gate
  and and_5 (beq, ~in_1[2], ~in_1[2], in_1[2], ~in_1[3], ~in_1[4], ~in_1[5]);  // AND_Gate
  and and_6 (bne, in_1[2], ~in_1[2], in_1[2], ~in_1[3], ~in_1[4], ~in_1[5]);  // AND_Gate
  and and_7 (jump, ~in_1[2], in_1[2], ~in_1[2], ~in_1[3], ~in_1[4], ~in_1[5]);  // AND_Gate
  and and_8 (isjal, in_1[2], in_1[2], ~in_1[2], ~in_1[3], ~in_1[4], ~in_1[5]);  // AND_Gate
  and and_9 (islui, in_1[2], in_1[2], in_1[2], in_1[3], ~in_1[4], ~in_1[5]);  // AND_Gate
  and and_10 (MemtoReg, in_1[2], in_1[2], ~in_1[2], ~in_1[3], ~in_1[4], in_1[5]);  // AND_Gate
  and and_11 (isori, in_1[2], ~in_1[2], in_1[2], in_1[3], ~in_1[4], ~in_1[5]);  // AND_Gate
  and and_12 (isslti, ~in_1[2], in_1[2], ~in_1[2], in_1[3], ~in_1[4], ~in_1[5]);  // AND_Gate
  and and_13 (issltiu, in_1[2], in_1[2], ~in_1[2], in_1[3], ~in_1[4], ~in_1[5]);  // AND_Gate
  and and_14 (MemWr, in_1[2], in_1[2], ~in_1[2], in_1[3], ~in_1[4], in_1[5]);  // AND_Gate
  and and_15 (isadd, RegDst, ~in_2[0], ~in_2[1], ~in_2[2], ~in_2[3], ~in_2[4], in_2[5]);  // AND_Gate
  and and_16 (isaddu, RegDst, in_2[0], ~in_2[1], ~in_2[2], ~in_2[3], ~in_2[4], in_2[5]);  // AND_Gate
  and and_17 (isand, RegDst, ~in_2[0], ~in_2[1], in_2[2], ~in_2[3], ~in_2[4], in_2[5]);  // AND_Gate
  and and_18 (isjr, RegDst, ~in_2[0], ~in_2[1], ~in_2[2], in_2[3], ~in_2[4], ~in_2[5]);  // AND_Gate
  and and_19 (isor, RegDst, in_2[0], ~in_2[1], in_2[2], ~in_2[3], ~in_2[4], in_2[5]);  // AND_Gate
  and and_20 (isslt, RegDst, ~in_2[0], in_2[1], ~in_2[2], in_2[3], ~in_2[4], in_2[5]);  // AND_Gate
  and and_21 (issltu, RegDst, in_2[0], in_2[1], ~in_2[2], in_2[3], ~in_2[4], in_2[5]);  // AND_Gate
  and and_22 (issll, RegDst, ~in_2[0], ~in_2[1], ~in_2[2], ~in_2[3], ~in_2[4], ~in_2[5]);  // AND_Gate
  and and_23 (issra, RegDst, in_2[0], in_2[1], ~in_2[2], ~in_2[3], ~in_2[4], ~in_2[5]);  // AND_Gate
  and and_24 (issrl, RegDst, ~in_2[0], in_2[1], ~in_2[2], ~in_2[3], ~in_2[4], ~in_2[5]);  // AND_Gate
  and and_25 (issub, RegDst, ~in_2[0], in_2[1], ~in_2[2], ~in_2[3], ~in_2[4], in_2[5]);  // AND_Gate
  and and_26 (issubu, RegDst, in_2[0], in_2[1], ~in_2[2], ~in_2[3], ~in_2[4], in_2[5]);  // AND_Gate
  and and_27 (jumpreg, RegDst, ~in_2[0], ~in_2[1], ~in_2[2], in_2[3], ~in_2[4], ~in_2[5]);  // AND_Gate
  or or_1 (RegWr, isaddiu, isori, RegDst, isaddi, isandi, MemtoReg, isslti, issltiu);
  or or_2 (ExtOp, isaddiu, MemtoReg, isaddi, isslti, issltiu, MemWr);
  or or_3 (ALUsrc, isaddiu, MemWr, isori, isaddi, isandi, MemtoReg, isslti, issltiu);
  or or_4 (or_4_out, MemWr, MemtoReg, isadd, isaddi);
  or or_5 (or_5_out, isslti, isslt);
  or or_6 (or_6_out, issltiu, issltu);
  or or_7 (or_7_out, isaddu, isaddiu);
  or or_8 (or_8_out, isand, isandi);
  or or_9 (or_9_out, isor, isori);
  Multiplexer #(.width(4)) multiplexer_1 (
    .in0(4'b0000), .in1(4'b0101), .out(multiplexer_1_out), .sel(or_4_out));  // open: en
  Multiplexer #(.width(4)) multiplexer_2 (
    .in0(4'b0000), .in1(4'b1011), .out(multiplexer_2_out), .sel(or_5_out));  // open: en
  Multiplexer #(.width(4)) multiplexer_3 (
    .in0(4'b0000), .in1(4'b1100), .out(multiplexer_3_out), .sel(or_6_out));  // open: en
  Multiplexer #(.width(4)) multiplexer_4 (
    .in0(4'b0000), .in1(4'b0110), .out(multiplexer_4_out), .sel(or_7_out));  // open: en
  Multiplexer #(.width(4)) multiplexer_5 (
    .in0(4'b0000), .in1(4'b1001), .out(multiplexer_5_out), .sel(or_8_out));  // open: en
  Multiplexer #(.width(4)) multiplexer_6 (
    .in0(4'b0000), .in1(4'b1010), .out(multiplexer_6_out), .sel(or_9_out));  // open: en
  Multiplexer #(.width(4)) multiplexer_7 (
    .in0(4'b0000), .in1(4'b0000), .out(multiplexer_7_out), .sel(issll));  // open: en
  Multiplexer #(.width(4)) multiplexer_8 (
    .in0(4'b0000), .in1(4'b0010), .out(multiplexer_8_out), .sel(issra));  // open: en
  Multiplexer #(.width(4)) multiplexer_9 (
    .in0(4'b0000), .in1(4'b0001), .out(multiplexer_9_out), .sel(issrl));  // open: en
  Multiplexer #(.width(4)) multiplexer_10 (
    .in0(4'b0000), .in1(4'b0111), .out(multiplexer_10_out), .sel(issub));  // open: en
  Multiplexer #(.width(4)) multiplexer_11 (
    .in0(4'b0000), .in1(4'b1000), .out(multiplexer_11_out), .sel(issubu));  // open: en
  assign ALUctr = multiplexer_1_out | multiplexer_2_out | multiplexer_3_out | multiplexer_4_out | multiplexer_5_out | multiplexer_6_out | multiplexer_7_out | multiplexer_8_out | multiplexer_9_out | multiplexer_10_out | multiplexer_11_out;  // OR_Gate or_10, 4 bits wide

  assign in_1[1:0] = {2{in_1[2]}};

  // Other names for the same wires on the sheet: funct[5:0] = in_2; isbeq = beq; isbne = bne; isjump = jump;
  //   isjumpreg = jumpreg; islw = MemtoReg; isrtype = RegDst; issw = MemWr; opcode[5:0] = {in_1[5:2], {2{in_1[2]}}}

  // Notes on the sheet:
  //   Determine the type of instruction:
  //   determine which r type instruction it is:
  //   INPUTS
  //   OUTPUTS
  //   Determine the control signals
  //   determine the ALUctr signal
endmodule
